# Fritzing sketch Segmentti (saved by Fritzing 0.9.3b)
circuit board: 8.46667cm x 5.64444cm
breadboards: 1

parts:
  Part1 = Arduino Uno (Rev3) - ICSP
  DI1 = 7-Segment LED Display [package=THT]
  R1 = Resistor [tolerance=±5% resistance=220 package=THT]
  R2 = Resistor [tolerance=±5% resistance=220 package=THT]
  R3 = Resistor [tolerance=±5% resistance=220 package=THT]
  R4 = Resistor [tolerance=±5% resistance=220 package=THT]
  R5 = Resistor [tolerance=±5% resistance=220 package=THT]
  R6 = Resistor [tolerance=±5% resistance=220 package=THT]
  R7 = Resistor [tolerance=±5% resistance=220 package=THT]
  R8 = Resistor [tolerance=±5% resistance=220 package=THT]

nets:
  N1: Part1.D8, R7.Pin_1
  N2: Part1.D9_PWM, R2.Pin_1
  N3: Part1.D10_PWM/SS, R4.Pin_1
  N4: Part1.D11_PWM/MOSI, R1.Pin_1
  N5: Part1.D4, R5.Pin_1
  N6: Part1.D5_PWM, R8.Pin_1
  N7: Part1.D6_PWM, R6.Pin_1
  N8: Part1.D7, R3.Pin_1
  N9: Part1.5V, DI1.commAnode#7
  N10: DI1.cathodeE, R1.Pin_0
  N11: DI1.cathodeD, R4.Pin_0
  N12: DI1.cathodeC, R2.Pin_0
  N13: DI1.cathodeDP, R7.Pin_0
  N14: DI1.cathodeB, R5.Pin_0
  N15: DI1.cathodeA, R8.Pin_0
  N16: DI1.cathodeF, R6.Pin_0
  N17: DI1.cathodeG, R3.Pin_0
